// Digital circuit CPU.dig as structural Verilog
module CPU (
  input  CLK,
  output [7:0] AC,
  output neg,
  output Over,
  output [7:0] MQ,
  output [7:0] N,
  output [2:0] OpCode,
  output [7:0] out_8,
  output [7:0] out_9
);

  wire button_1_out, IR, MAROperando, \MAROperação , PC, PC_ovf;
  wire [2:0] driver_5_out;
  wire [7:0] AC_t, IR_q, MAROperandos_q, \MAROperações_q , MQ_t;

  Register #(.Bits(8)) MAROperandos (.D(out_8), .C(CLK), .en(1'b1), .Q(MAROperandos_q));
  EEPROMDualPort #(.AddrBits(8), .Bits(8)) Operandos (
    .A(out_8), .Din({8{1'b0}}), .str(1'b0), .C(CLK), .ld(1'b1), .D(N));
  Button button_1 (.out(button_1_out));
  Counter #(.Bits(8)) u_PC (.en(PC), .C(CLK), .clr(1'b0), .out(out_9), .ovf(PC_ovf));
  Register #(.Bits(8)) u_IR (.D({{5{1'b0}}, OpCode}), .C(CLK), .en(1'b1), .Q(IR_q));
  ControlUnit CC (
    .CLK(CLK), .bt(button_1_out), .PC(PC), .\MAROperação (\MAROperação ), .MAROperando(MAROperando), .IR(IR));
  assign out_8 = MAROperando ? MAROperandos_q : 8'bz;  // Driver driver_1
  assign out_8 = PC ? out_9 : 8'bz;  // Driver driver_2
  assign out_8 = IR ? IR_q : 8'bz;  // Driver driver_3
  Register #(.Bits(8)) \MAROperações  (.D(out_8), .C(CLK), .en(1'b1), .Q(\MAROperações_q ));
  EEPROMDualPort #(.AddrBits(8), .Bits(3)) \Operações  (
    .A(out_8), .Din(3'b000), .str(1'b0), .C(CLK), .ld(1'b1), .D(OpCode));
  assign out_8 = \MAROperação  ? \MAROperações_q  : 8'bz;  // Driver driver_4
  assign driver_5_out = IR ? out_8[2:0] : 3'bz;  // Driver driver_5
  Register #(.Bits(8)) u_AC (.D(AC_t), .C(CLK), .en(1'b1), .Q(AC));
  ALU8bits ALU (.N(N), .S(driver_5_out), .CLK(CLK), .MQ(MQ_t), .neg(neg), .AC(AC_t), .Over(Over));
  Register #(.Bits(8)) u_MQ (.D(MQ_t), .C(CLK), .en(1'b1), .Q(MQ));
  // also tied to GND on the sheet: PC_ovf

  // Other names for the same wires on the sheet: BUS[7:0] = out_8; IROp[2:0] = OpCode

  // Notes on the sheet:
  //   contents of Operandos (hex, n*v repeats v):
  //   1,2,3,4,5,6
endmodule
