// Digital circuit soma1bit.dig as structural Verilog
module soma1bit (
  input  A,
  input  B,
  input  Cin,
  output S,
  output Cout
);

  wire and_1_out, and_2_out, and_3_out;

  xor xor_1 (S, Cin, A, B);
  and and_1 (and_1_out, Cin, A);
  and and_2 (and_2_out, Cin, B);
  and and_3 (and_3_out, A, B);
  or or_1 (Cout, and_1_out, and_2_out, and_3_out);
endmodule
